# Fritzing sketch LaserBasin (saved by Fritzing 0.9.3b)
circuit board: 3.55cm x 2.54cm
breadboards: 1
perfboards: 1

parts:
  Part1 = Arduino Mega 2560 (Rev3)
  R4 = Resistor [tolerance=±5% resistance=220 package=THT]
  LED1 = LED - 5mm [color="Red (633nm)" package="5 mm [THT]"]
  R1 = Resistor [tolerance=±5% resistance=220 package=THT]
  R2 = Resistor [tolerance=±5% resistance=220 package=THT]
  R3 = Resistor [tolerance=±5% resistance=220 package=THT]
  LED2 = LED - 5mm [color="Green (555nm)" package="5 mm [THT]"]
  LED3 = LED - 5mm [color="Green (555nm)" package="5 mm [THT]"]
  LED4 = LED - 5mm [color="Green (555nm)" package="5 mm [THT]"]
  R5 = Photocell (LDR) [package=THT]  # not connected
  J1 = Piezo Speaker  # not connected
  U2 = L298 [package=multiwatt15]  # not connected
  M1 = DC Motor  # not connected
  M2 = DC Motor  # not connected
  J2 = male pin header, 5 pins [form="♂ (male)"]

nets:
  N1: Part1.GND, LED1.cathode, LED2.cathode, LED3.cathode, LED4.cathode, J2.pin5
  N2: Part1.D23, R1.Pin_0, J2.pin1
  N3: Part1.D25, R2.Pin_0, J2.pin2
  N4: Part1.D27, R3.Pin_0, J2.pin3
  N5: Part1.D29, R4.Pin_0, J2.pin4
  N6: R4.Pin_1, LED4.anode
  N7: LED1.anode, R1.Pin_1
  N8: R2.Pin_1, LED2.anode
  N9: R3.Pin_1, LED3.anode

notes:
  Health indicator
