# Fritzing sketch Talas (saved by Fritzing 0.9.3b)
circuit board: 2.54cm x 1.5cm
circuit board: 3.4cm x 2cm
perfboards: 2

parts:
  U1 = Arduino Mega 2560 (Rev3)
  R4 = Resistor [tolerance=±5% resistance=220 package=THT]
  LED1 = LED - 5mm [color="Red (633nm)" package="5 mm [THT]"]
  R1 = Resistor [tolerance=±5% resistance=220 package=THT]
  R2 = Resistor [tolerance=±5% resistance=220 package=THT]
  R3 = Resistor [tolerance=±5% resistance=220 package=THT]
  LED2 = LED - 5mm [color="Green (555nm)" package="5 mm [THT]"]
  LED3 = LED - 5mm [color="Green (555nm)" package="5 mm [THT]"]
  LED4 = LED - 5mm [color="Green (555nm)" package="5 mm [THT]"]
  U2 = L298 [package=multiwatt15]
  M1 = DC Motor
  M2 = DC Motor
  J9 = male pin header, 5 pins [form="♂ (male)"]
  R5 = Photocell (LDR) [package=THT]
  J10 = male pin header, 3 pins [form="♂ (male)"]
  R6 = Resistor [tolerance=±5% resistance=10k package=THT]
  U3 = Bluetooth HC-05 Macho
  R8 = Resistor [tolerance=±5% resistance=10k package=THT]
  R7 = Photocell (LDR) [package=THT]
  R9 = Photocell (LDR) [package=THT]
  R10 = Resistor [tolerance=±5% resistance=10k package=THT]
  R11 = Photocell (LDR) [package=THT]
  R12 = Resistor [tolerance=±5% resistance=10k package=THT]
  U4 = mystery part, 3 pins [chip_label=Laser]
  V2 = DC Power [voltage=12V frequency=60]
  Part1 = Arduino Mega Proto Shield (v6)
  J2 = male pin header, 6 pins [form="♂ (male)"]
  J8 = male pin header, 3 pins [form="♂ (male)"]
  J7 = male pin header, 3 pins [form="♂ (male)"]
  J6 = male pin header, 3 pins [form="♂ (male)"]
  J5 = male pin header, 3 pins [form="♂ (male)"]
  U5 = Basic Servo
  U6 = Basic Servo
  J1 = Screw terminal - 2 pins [package=THT]
  J3 = female pin header, 6 pins [form="♀ (female)"]
  J4 = male pin header, 5 pins [form="♂ (male)"]
  J12 = male pin header, 6 pins [form="♂ (male)"]

nets (from the schematic view):
  5V: U1.5V, U2.VLS, R5.pin_1, J10.pin2, U3.VCC, R7.pin_1, R9.pin_1, R11.pin_1, U4.pin2, Part1.+5V, Part1.N$44, Part1.N$250, Part1.N$253, Part1.N$254, Part1.N$341, Part1.N$463, J8.pin2, J7.pin2, J6.pin2, J5.pin2, U5.vcc, U6.vcc, J1.pin1, J3.pin2
  GND: U1.GND, LED1.cathode, LED2.cathode, LED3.cathode, LED4.cathode, U2.GND, J9.pin5, J10.pin3, R6.Pin_1, U3.GND, R8.Pin_1, R10.Pin_1, R12.Pin_1, U4.pin3, V2.V-, Part1.N$40, Part1.N$51, Part1.N$213, Part1.N$214, Part1.N$215, Part1.N$301, Part1.N$462, J8.pin3, J7.pin3, J6.pin3, J5.pin3, U5.gnd, U6.gnd, J1.pin2, J3.pin3, J4.pin5
  Health 3: R4.Pin_0, J9.pin4, Part1.D48, Part1.N$466, J4.pin4
  N1: R4.Pin_1, LED4.anode
  N2: LED1.anode, R1.Pin_1
  Health 0: R1.Pin_0, J9.pin1, Part1.D42, Part1.N$345, J4.pin1
  Health 1: R2.Pin_0, J9.pin2, Part1.D44, Part1.N$447, J4.pin2
  N3: R2.Pin_1, LED2.anode
  Health 2: R3.Pin_0, J9.pin3, Part1.D46, Part1.N$458, J4.pin3
  N4: R3.Pin_1, LED3.anode
  N5: U2.OUT1, M1.pin_1
  N6: U2.OUT2, M1.pin_2
  N7: U2.VS, V2.V+
  in1: U2.IN1, Part1.D28, Part1.N$80, J2.pin2
  enA: U2.ENA, Part1.D11, Part1.N$68, J2.pin1
  in2: U2.IN2, Part1.D30, Part1.N$29, J2.pin3
  in3: U2.IN3, Part1.D32, Part1.N$92, J2.pin4
  enB: U2.ENB, Part1.D12, Part1.N$30, J2.pin6
  in4: U2.IN4, Part1.D34, Part1.N$35, J2.pin5
  N8: U2.OUT3, M2.pin_1
  N9: U2.OUT4, M2.pin_2
  hit: R5.pin_0, J10.pin1, R6.Pin_0, R8.Pin_0, R7.pin_0, R9.pin_0, R10.Pin_0, R11.pin_0, R12.Pin_0
  BT state: U3.State, Part1.D26, Part1.N$206, J3.pin6
  TX: U3.TXD, Part1.RX1, Part1.N$256, J3.pin4
  RX: U3.RXD, Part1.TX1, Part1.N$217, J3.pin5
  BT key: U3.Key, Part1.D24, Part1.N$352, J3.pin1
  Laser: U4.pin1, Part1.D36, Part1.N$270, J6.pin1
  Hit: Part1.A12, Part1.N$464, J5.pin1
  Servo H: Part1.D38, Part1.N$287, J7.pin1, U5.pulse
  Servo V: Part1.D40, Part1.N$288, J8.pin1, U6.pulse
  N10: Part1.N$207, J12.pin6
  N11: Part1.N$218, J12.pin5
  N12: Part1.N$257, J12.pin4
  N13: Part1.N$302, J12.pin3
  N14: Part1.N$342, J12.pin2
  N15: Part1.N$382, J12.pin1

notes:
  TALAS, Health indicator, 1
  TALAS, Hit detector, 1
  TALAS, Driver L298N, DC motors, and 12V power, 1
  TALAS, Turret with laser gun, 1
  S
  G
  1
  2
  3
  4
  0
  Health
  Hit
  TALAS, Bluetooth module, 1
  TALAS, Arduino Mega 2560 Rev3 with shield, 1
